// Logisim project cpu_xor.circ as structural Verilog: 10 circuits, main circuit main
module main (
  input  in_1,
  output [31:0] out_2,
  output [31:0] out_3,
  output out_4,
  output [4:0] out_5,
  output [31:0] out_6,
  output out_7,
  output [31:0] out_8,
  output [31:0] out_9
);

  wire alu_1_a____b, clk, control_1_out_5, control_1_out_6;
  wire [1:0] control_1_out_8, control_1_out_9, control_1_out_10, control_1_out_11, control_1_out_12;
  wire [4:0] spl_1_rd, spl_1_rs, spl_1_rt;
  wire [5:0] spl_1_out_2, spl_1_out_7;
  wire [15:0] spl_1_out_8;
  wire [25:0] spl_1_out_9;
  wire [31:0] dm_1_out_6, ext_1_out_3, grf_1_out_8, multiplexer_2_out, npc_1_out_5, PC_4;

  Clock clock_1 (.out(clk));
  PC pc_1 (.in_1(32'h3000), .in_2(npc_1_out_5), .in_3(clk), .in_4(in_1), .out_5(out_3));
  NPC npc_1 (.in_2(out_3), .in_3(spl_1_out_9), .out_5(npc_1_out_5), .in_1(control_1_out_8), .out_4(PC_4));
  IM im_1 (.in_1(out_3), .out_2(out_2));
  SPL spl_1 (
    .in_1(out_2), .out_2(spl_1_out_2), .rs(spl_1_rs), .rt(spl_1_rt), .rd(spl_1_rd), .out_7(spl_1_out_7),
    .out_8(spl_1_out_8), .out_9(spl_1_out_9));  // open: shamt
  Control control_1 (
    .opcode(spl_1_out_2), .funct(spl_1_out_7), .out_8(control_1_out_8), .out_10(control_1_out_10),
    .out_4(out_4), .out_5(control_1_out_5), .out_6(control_1_out_6), .out_7(out_7),
    .out_11(control_1_out_11), .out_12(control_1_out_12), .out_9(control_1_out_9), .flag(alu_1_a____b));
  Multiplexer #(.select(2), .width(5), .enable("false")) multiplexer_1 (
    .in0(spl_1_rt), .in1(spl_1_rd), .in2({5{1'b1}}), .out(out_5), .sel(control_1_out_10));  // open: in3
  EXT ext_1 (.in_2(spl_1_out_8), .out_3(ext_1_out_3), .in_1(control_1_out_9));
  GRF grf_1 (
    .in_1(clk), .in_2(in_1), .in_3(out_4), .in_4(spl_1_rs), .in_5(spl_1_rt), .in_6(out_5), .in_7(out_6),
    .out_8(grf_1_out_8), .out_9(out_9));
  Multiplexer #(.width(32), .enable("false")) multiplexer_2 (
    .in0(out_9), .in1(ext_1_out_3), .out(multiplexer_2_out), .sel(control_1_out_5));
  ALU alu_1 (
    .in_3(grf_1_out_8), .in_4(multiplexer_2_out), .out_5(out_8), .A____B(alu_1_a____b),
    .in_1(control_1_out_6), .in_2(control_1_out_12));
  DM dm_1 (.in_1(out_8), .in_2(clk), .in_3(out_9), .in_4(out_7), .in_5(in_1), .out_6(dm_1_out_6));
  Multiplexer #(.select(2), .width(32), .enable("false")) multiplexer_3 (
    .in0(out_8), .in1(dm_1_out_6), .in2(PC_4), .out(out_6), .sel(control_1_out_11));  // open: in3

  // Other names for the same wires on the sheet: Instr[31:0] = out_2; MemAddr[31:0] = out_8; MemData[31:0] = out_9;
  //   MemWrite = out_7; PC[31:0] = out_3; RegAddr[4:0] = out_5; RegData[31:0] = out_6; RegWrite = out_4; rst = in_1

  // Notes on the sheet:
  //   IM_slt
  //   A3_slt
  //   GRF_we
  //   B_slt
  //   cal_slt
  //   out_slt
  //   DM_we
endmodule

module ALU (
  input  in_1,
  input  [1:0] in_2,
  input  [31:0] in_3,
  input  [31:0] in_4,
  output [31:0] out_5,
  output A____B
);

  wire [31:0] adder_1_out, multiplexer_1_out, not_1_out, or_1_out, xor_1_out;

  assign not_1_out = ~in_4;  // NOT_Gate not_1, 32 bits wide
  Multiplexer #(.width(32), .enable("false")) multiplexer_1 (
    .in0(in_4), .in1(not_1_out), .out(multiplexer_1_out), .sel(in_1));
  Adder #(.width(32)) adder_1 (.a(in_3), .b(multiplexer_1_out), .out(adder_1_out), .cin(in_1));  // open: cout
  Comparator #(.width(32), .mode("unsigned")) comparator_1 (.a(in_3), .b(in_4), .eq(A____B));  // open: gt, lt
  assign or_1_out = in_3 | in_4;  // OR_Gate or_1, 32 bits wide
  assign xor_1_out = in_3 ^ in_4;  // XOR_Gate xor_1, 32 bits wide
  Multiplexer #(.select(2), .width(32), .enable("false")) multiplexer_2 (
    .in0(adder_1_out), .in1(or_1_out), .in2(in_4), .in3(xor_1_out), .out(out_5), .sel(in_2));

  // Other names for the same wires on the sheet: A[31:0] = in_3; B[31:0] = in_4; cal_slt = in_1; out_slt[1:0] = in_2

  // Notes on the sheet:
  //   A
  //   B
  //   A+B/A-B
  //   A or B
  //   B
  //   A xor B
endmodule

module GRF (
  input  in_1,
  input  in_2,
  input  in_3,
  input  [4:0] in_4,
  input  [4:0] in_5,
  input  [4:0] in_6,
  input  [31:0] in_7,
  output [31:0] out_8,
  output [31:0] out_9
);

  wire multiplexer_1_out, we_1, we_2, we_3, we_4, we_5, we_6, we_7, we_8, we_9, we_10, we_11, we_12, we_13,
       we_14, we_15, we_16, we_17, we_18, we_19, we_20, we_21, we_22, we_23, we_24, we_25, we_26, we_27,
       we_28, we_29, we_30, we_31;
  wire [31:0] rd_1_t, rd_2_t, rd_3, rd_4, rd_5, rd_6, rd_7, rd_8, rd_9, rd_10, rd_11, rd_12, rd_13, rd_14,
       rd_15, rd_16, rd_17, rd_18, rd_19, rd_20, rd_21, rd_22, rd_23, rd_24, rd_25, rd_26, rd_27, rd_28,
       rd_29, rd_30, rd_31, write_1, write_2, write_3, write_4, write_5, write_6, write_7, write_8, write_9,
       write_10, write_11, write_12, write_13, write_14, write_15, write_16, write_17, write_18, write_19,
       write_20, write_21, write_22, write_23, write_24, write_25, write_26, write_27, write_28, write_29,
       write_30, write_31;

  Multiplexer #(.enable("false")) multiplexer_1 (.in0(1'b0), .in1(1'b1), .out(multiplexer_1_out), .sel(in_3));
  Demultiplexer #(.select(5), .enable("false")) demultiplexer_1 (
    .out1(we_1), .out2(we_2), .out3(we_3), .out4(we_4), .out5(we_5), .out6(we_6), .out7(we_7), .out8(we_8),
    .out9(we_9), .out10(we_10), .out11(we_11), .out12(we_12), .out13(we_13), .out14(we_14), .out15(we_15),
    .out16(we_16), .out17(we_17), .out18(we_18), .out19(we_19), .out20(we_20), .out21(we_21), .out22(we_22),
    .out23(we_23), .out24(we_24), .out25(we_25), .out26(we_26), .out27(we_27), .out28(we_28), .out29(we_29),
    .out30(we_30), .out31(we_31), .in(multiplexer_1_out), .sel(in_6));  // open: out0
  Register #(.width(32)) _1 (.D(write_1), .en(we_1), .Q(rd_1_t), .clk(in_1), .clr(in_2));
  Register #(.width(32)) _2 (.D(write_2), .en(we_2), .Q(rd_2_t), .clk(in_1), .clr(in_2));
  Register #(.width(32)) _3 (.D(write_3), .en(we_3), .Q(rd_3), .clk(in_1), .clr(in_2));
  Register #(.width(32)) _4 (.D(write_4), .en(we_4), .Q(rd_4), .clk(in_1), .clr(in_2));
  Register #(.width(32)) _5 (.D(write_5), .en(we_5), .Q(rd_5), .clk(in_1), .clr(in_2));
  Register #(.width(32)) _6 (.D(write_6), .en(we_6), .Q(rd_6), .clk(in_1), .clr(in_2));
  Register #(.width(32)) _7 (.D(write_7), .en(we_7), .Q(rd_7), .clk(in_1), .clr(in_2));
  Multiplexer #(.select(5), .width(32), .enable("false")) multiplexer_2 (
    .in0({32{1'b0}}), .in1(rd_1_t), .in2(rd_2_t), .in3(rd_3), .in4(rd_4), .in5(rd_5), .in6(rd_6), .in7(rd_7),
    .in8(rd_8), .in9(rd_9), .in10(rd_10), .in11(rd_11), .in12(rd_12), .in13(rd_13), .in14(rd_14),
    .in15(rd_15), .in16(rd_16), .in17(rd_17), .in18(rd_18), .in19(rd_19), .in20(rd_20), .in21(rd_21),
    .in22(rd_22), .in23(rd_23), .in24(rd_24), .in25(rd_25), .in26(rd_26), .in27(rd_27), .in28(rd_28),
    .in29(rd_29), .in30(rd_30), .in31(rd_31), .out(out_8), .sel(in_4));
  Register #(.width(32)) _8 (.D(write_8), .en(we_8), .Q(rd_8), .clk(in_1), .clr(in_2));
  Register #(.width(32)) _9 (.D(write_9), .en(we_9), .Q(rd_9), .clk(in_1), .clr(in_2));
  Register #(.width(32)) _10 (.D(write_10), .en(we_10), .Q(rd_10), .clk(in_1), .clr(in_2));
  Register #(.width(32)) _11 (.D(write_11), .en(we_11), .Q(rd_11), .clk(in_1), .clr(in_2));
  Register #(.width(32)) _12 (.D(write_12), .en(we_12), .Q(rd_12), .clk(in_1), .clr(in_2));
  Register #(.width(32)) _13 (.D(write_13), .en(we_13), .Q(rd_13), .clk(in_1), .clr(in_2));
  Register #(.width(32)) _14 (.D(write_14), .en(we_14), .Q(rd_14), .clk(in_1), .clr(in_2));
  Register #(.width(32)) _15 (.D(write_15), .en(we_15), .Q(rd_15), .clk(in_1), .clr(in_2));
  Register #(.width(32)) _16 (.D(write_16), .en(we_16), .Q(rd_16), .clk(in_1), .clr(in_2));
  Register #(.width(32)) _17 (.D(write_17), .en(we_17), .Q(rd_17), .clk(in_1), .clr(in_2));
  Register #(.width(32)) _18 (.D(write_18), .en(we_18), .Q(rd_18), .clk(in_1), .clr(in_2));
  Register #(.width(32)) _19 (.D(write_19), .en(we_19), .Q(rd_19), .clk(in_1), .clr(in_2));
  Register #(.width(32)) _20 (.D(write_20), .en(we_20), .Q(rd_20), .clk(in_1), .clr(in_2));
  Register #(.width(32)) _21 (.D(write_21), .en(we_21), .Q(rd_21), .clk(in_1), .clr(in_2));
  Register #(.width(32)) _22 (.D(write_22), .en(we_22), .Q(rd_22), .clk(in_1), .clr(in_2));
  Register #(.width(32)) _23 (.D(write_23), .en(we_23), .Q(rd_23), .clk(in_1), .clr(in_2));
  Multiplexer #(.select(5), .width(32), .enable("false")) multiplexer_3 (
    .in0({32{1'b0}}), .in1(rd_1_t), .in2(rd_2_t), .in3(rd_3), .in4(rd_4), .in5(rd_5), .in6(rd_6), .in7(rd_7),
    .in8(rd_8), .in9(rd_9), .in10(rd_10), .in11(rd_11), .in12(rd_12), .in13(rd_13), .in14(rd_14),
    .in15(rd_15), .in16(rd_16), .in17(rd_17), .in18(rd_18), .in19(rd_19), .in20(rd_20), .in21(rd_21),
    .in22(rd_22), .in23(rd_23), .in24(rd_24), .in25(rd_25), .in26(rd_26), .in27(rd_27), .in28(rd_28),
    .in29(rd_29), .in30(rd_30), .in31(rd_31), .out(out_9), .sel(in_5));
  Demultiplexer #(.select(5), .width(32), .enable("false")) demultiplexer_2 (
    .out1(write_1), .out2(write_2), .out3(write_3), .out4(write_4), .out5(write_5), .out6(write_6),
    .out7(write_7), .out8(write_8), .out9(write_9), .out10(write_10), .out11(write_11), .out12(write_12),
    .out13(write_13), .out14(write_14), .out15(write_15), .out16(write_16), .out17(write_17),
    .out18(write_18), .out19(write_19), .out20(write_20), .out21(write_21), .out22(write_22),
    .out23(write_23), .out24(write_24), .out25(write_25), .out26(write_26), .out27(write_27),
    .out28(write_28), .out29(write_29), .out30(write_30), .out31(write_31), .in(in_7), .sel(in_6));  // open: out0
  Register #(.width(32)) _24 (.D(write_24), .en(we_24), .Q(rd_24), .clk(in_1), .clr(in_2));
  Register #(.width(32)) _25 (.D(write_25), .en(we_25), .Q(rd_25), .clk(in_1), .clr(in_2));
  Register #(.width(32)) _26 (.D(write_26), .en(we_26), .Q(rd_26), .clk(in_1), .clr(in_2));
  Register #(.width(32)) _27 (.D(write_27), .en(we_27), .Q(rd_27), .clk(in_1), .clr(in_2));
  Register #(.width(32)) _28 (.D(write_28), .en(we_28), .Q(rd_28), .clk(in_1), .clr(in_2));
  Register #(.width(32)) _29 (.D(write_29), .en(we_29), .Q(rd_29), .clk(in_1), .clr(in_2));
  Register #(.width(32)) _30 (.D(write_30), .en(we_30), .Q(rd_30), .clk(in_1), .clr(in_2));
  Register #(.width(32)) _31 (.D(write_31), .en(we_31), .Q(rd_31), .clk(in_1), .clr(in_2));

  // Other names for the same wires on the sheet: adder_1[4:0] = in_4; adder_2[4:0] = in_5; adder_3[4:0] = in_6;
  //   clk = in_1; RD_1[31:0] = out_8; RD_2[31:0] = out_9; rst = in_2; we = in_3; write[31:0] = in_7
endmodule

module PC (
  input  [31:0] in_1,
  input  [31:0] in_2,
  input  in_3,
  input  in_4,
  output [31:0] out_5
);

  wire [31:0] register_1_q, xor_1_out;

  assign xor_1_out = in_1 ^ in_2;  // XOR_Gate xor_1, 32 bits wide
  Register #(.width(32)) register_1 (.D(xor_1_out), .Q(register_1_q), .clk(in_3), .clr(in_4));  // open: en
  assign out_5 = in_1 ^ register_1_q;  // XOR_Gate xor_2, 32 bits wide
endmodule

module NPC (
  input  [1:0] in_1,
  input  [31:0] in_2,
  input  [25:0] in_3,
  output [31:0] out_4,
  output [31:0] out_5
);

  wire [31:0] adder_2_out, bit_extender_1_out;

  // Probe on bit_extender_1_out
  assign bit_extender_1_out = {{14{in_3[15]}}, {in_3[15:0], 2'b00}};  // Bit_Extender bit_extender_1
  Adder #(.width(32)) adder_1 (.a(in_2), .b(32'h4), .out(out_4));  // open: cin, cout
  Adder #(.width(32)) adder_2 (.a(out_4), .b(bit_extender_1_out), .out(adder_2_out));  // open: cin, cout
  Multiplexer #(.select(2), .width(32), .enable("false")) multiplexer_1 (
    .in0(out_4), .in1(adder_2_out), .in2({in_2[31:28], in_3, 2'b00}), .out(out_5), .sel(in_1));  // open: in3

  // Other names for the same wires on the sheet: imm_i[15:0] = in_3[15:0]; imm_j[25:0] = in_3; PC[31:0] = in_2;
  //   im_slt[1:0] = in_1
endmodule

module IM (
  input  [31:0] in_1,
  output [31:0] out_2
);

  wire [31:0] shifter_1_out, subtractor_1_out;

  Subtractor #(.width(32)) subtractor_1 (.a(in_1), .b(32'h3000), .out(subtractor_1_out));  // open: bin, bout
  // Probe on shifter_1_out[11:0]
  Shifter #(.width(32), .shift("lr")) shifter_1 (.in(subtractor_1_out), .\dist (5'b00010), .out(shifter_1_out));
  ROM #(.addrWidth(12), .dataWidth(32)) rom_1 (.addr(shifter_1_out[11:0]), .data(out_2));  // open: sel

  // Notes on the sheet:
  //   contents of rom_1 (hex, n*v repeats v):
  //   3400000b 34010004 3402000b 34030009 34040007 34050003 34060007 34070009 34080007 34090003 340a0007
  //   340b000a 340c000b 340d0003 340e000b 340f0009 3410000b 3411000b 34120004 34130009 3414000c 34150007
  //   34160004 3417000c 3418000a 34190007 341a0007 341b000a 341c0005 341d0008 341e000c 3c190086 c000c21
  //   3c0affff 354a0000 3c19ffff 37390001 372afffd 340a0008 34190006 340e0008 8dcf0050 34a60000 0 0
  //   15e4820 105e822 340f00ac 3c0affff 354a0001 3c15ffff 36b50000 3c10ffff 3610fffd 1558022 340a0007
  //   3415000c 3410000c 3c0400b9 1355820 34170014 8ef80064 3c13ffff 3673fffd 3c0bffff 356bfffe 3573ffff
  //   34130009 340b0008 340c000c 8d8d003c 0 34020014 8c410094 3c0effff 35ce0002 3c0cffff 358c0000 3c11ffff
  //   36310001 1cc8820 340e000b 340c0005 34110006 34000018 8c090014
endmodule

module DM (
  input  [31:0] in_1,
  input  in_2,
  input  [31:0] in_3,
  input  in_4,
  input  in_5,
  output [31:0] out_6
);

  wire [31:0] shifter_1_out;

  Shifter #(.width(32), .shift("lr")) shifter_1 (.in(in_1), .\dist (5'b00010), .out(shifter_1_out));
  RAM #(.addrWidth(12), .dataWidth(32), .bus("separate")) ram_1 (
    .addr(shifter_1_out[11:0]), .din(in_3), .data(out_6), .str(in_4), .clk(in_2), .clr(in_5));  // open: sel, ld
endmodule

module Control (
  input  [5:0] opcode,
  input  [5:0] funct,
  input  flag,
  output out_4,
  output out_5,
  output out_6,
  output out_7,
  output [1:0] out_8,
  output [1:0] out_9,
  output [1:0] out_10,
  output [1:0] out_11,
  output [1:0] out_12
);

  wire add, beq, beq_t, jal, lui, lw, nop, not_1_out, not_2_out, not_3_out, not_4_out, not_5_out, not_6_out,
       not_7_out, not_8_out, not_9_out, not_10_out, not_11_out, not_12_out, ori, R_type, sub, sw, \xor ;

  and and_1 (beq_t, flag, beq);
  buf IM_slt0 (out_8[0], beq_t);  // OR_Gate
  not not_1 (not_1_out, opcode[0]);
  not not_2 (not_2_out, opcode[1]);
  not not_3 (not_3_out, opcode[2]);
  not not_4 (not_4_out, opcode[3]);
  not not_5 (not_5_out, opcode[4]);
  not not_6 (not_6_out, opcode[5]);
  and and_2 (R_type, not_1_out, not_2_out, not_3_out, not_4_out, not_5_out, not_6_out);
  not not_7 (not_7_out, funct[0]);
  not not_8 (not_8_out, funct[1]);
  not not_9 (not_9_out, funct[2]);
  not not_10 (not_10_out, funct[3]);
  not not_11 (not_11_out, funct[4]);
  not not_12 (not_12_out, funct[5]);
  and and_3 (add, R_type, not_8_out, not_9_out, not_10_out, not_11_out, funct[5]);
  buf IM_slt1 (out_8[1], jal);  // OR_Gate
  and and_4 (ori, opcode[0], not_2_out, opcode[2], opcode[3], not_5_out, not_6_out);
  and and_5 (sub, R_type, funct[1], not_9_out, not_10_out, not_11_out, funct[5]);
  or ext_slt0 (out_9[0], sw, lw);
  and and_6 (nop, R_type, not_7_out, not_8_out, not_9_out, not_10_out, not_11_out, not_12_out);
  buf ext_slt1 (out_9[1], lui);  // OR_Gate
  and and_7 (lui, opcode[0], opcode[1], opcode[2], opcode[3], not_5_out, not_6_out);
  buf A3_slt (out_10[0], R_type);  // OR_Gate
  and and_8 (lw, opcode[0], opcode[1], not_3_out, not_4_out, not_5_out, opcode[5]);
  and and_9 (\xor , R_type, not_7_out, funct[1], funct[2], not_10_out, not_11_out, funct[5]);
  buf A3_slt1 (out_10[1], jal);  // OR_Gate
  and and_10 (sw, opcode[0], opcode[1], not_3_out, opcode[3], not_5_out, opcode[5]);
  or GRF_we (out_4, \xor , sub, lui, add, lw, ori, jal);
  and and_11 (beq, not_1_out, not_2_out, opcode[2], not_4_out, not_5_out, not_6_out);
  or B_slt (out_5, ori, lui, lw, sw);
  and and_12 (jal, opcode[0], opcode[1], not_3_out, not_4_out, not_5_out, not_6_out);
  buf cal_slt (out_6, sub);  // OR_Gate
  or out_slt0 (out_12[0], ori, \xor );
  or out_slt1 (out_12[1], lui, \xor );
  buf DM_we (out_7, sw);  // OR_Gate
  buf WD_slt (out_11[0], lw);  // OR_Gate
  buf WD_slt1 (out_11[1], jal);  // OR_Gate
endmodule

module SPL (
  input  [31:0] in_1,
  output [5:0] out_2,
  output [4:0] rs,
  output [4:0] rt,
  output [4:0] rd,
  output [4:0] shamt,
  output [5:0] out_7,
  output [15:0] out_8,
  output [25:0] out_9
);


  assign out_2 = in_1[31:26];
  assign out_7 = in_1[5:0];
  assign out_8 = in_1[15:0];
  assign out_9 = in_1[25:0];
  assign rd = in_1[15:11];
  assign rs = in_1[25:21];
  assign rt = in_1[20:16];
  assign shamt = in_1[10:6];

  // Other names for the same wires on the sheet: IM[31:0] = in_1

  // Notes on the sheet:
  //   R
  //   I
  //   J
  //   funct
  //   opcode
  //   offset
  //   offset_j
endmodule

module EXT (
  input  [1:0] in_1,
  input  [15:0] in_2,
  output [31:0] out_3
);

  wire [31:0] bit_extender_1_out, bit_extender_2_out;

  assign bit_extender_1_out = {{16{1'b0}}, in_2};  // Bit_Extender bit_extender_1
  assign bit_extender_2_out = {{16{in_2[15]}}, in_2};  // Bit_Extender bit_extender_2
  Multiplexer #(.select(2), .width(32), .enable("false")) multiplexer_1 (
    .in0(bit_extender_1_out), .in1(bit_extender_2_out), .in2({in_2, {16{1'b0}}}), .out(out_3), .sel(in_1));  // open: in3

  // Other names for the same wires on the sheet: ext_slt[1:0] = in_1

  // Notes on the sheet:
  //   imm
endmodule
