// Logisim project gfcpu.circ as structural Verilog: 8 circuits, main circuit main
module main (
  input  in_1,
  output [31:0] out_2,
  output [31:0] out_3,
  output out_4,
  output [31:0] out_5,
  output [31:0] out_6,
  output out_7,
  output [4:0] out_8,
  output [31:0] out_9
);

  wire Bsel, clk, ctrl_1_out_11, LessZero, WDsel, WRsel, Zero;
  wire [1:0] EXTop;
  wire [2:0] ALUop, NPCop;
  wire [31:0] dm_1_rd, ext_1_out_3, grf_1_rd1, multiplexer_3_out, npc_1_npc, pc, ra;

  Clock clock_1 (.out(clk));
  IFU ifu_1 (.Instr(out_3), .NPC(npc_1_npc), .clk(clk), .reset(in_1), .out_5(pc));
  NPC npc_1 (.PC(pc), .Imm(out_3[25:0]), .Zero(Zero), .NPC(npc_1_npc), .rs(ra), .NPCop(NPCop));
  // Probe on npc_1_npc
  Adder #(.width(32)) adder_1 (.a(pc), .b(32'h3000), .out(out_5));  // open: cin, cout
  Multiplexer #(.width(5)) multiplexer_1 (
    .in0(out_3[15:11]), .in1(out_3[20:16]), .out(out_8), .sel(WRsel));  // open: en
  CTRL ctrl_1 (
    .OPcode(out_3[31:26]), .Funct(out_3[5:0]), .out_9(ALUop), .out_10(NPCop), .out_3(WRsel), .out_4(WDsel),
    .out_5(out_7), .out_6(Bsel), .out_7(out_4), .out_8(EXTop), .out_11(ctrl_1_out_11));
  Multiplexer #(.width(32)) multiplexer_2 (.in0(dm_1_rd), .in1(out_6), .out(out_2), .sel(WDsel));  // open: en
  EXT ext_1 (._0_15(out_3[15:0]), .out_3(ext_1_out_3), .EXTop(EXTop));
  GRF grf_1 (
    .in_2(out_3[25:21]), .in_3(out_3[20:16]), .in_4(out_8), .in_5(out_2), .RD1(grf_1_rd1), .RD2(out_9),
    .in_1(out_7), .in_7(in_1), .in_6(clk));
  Multiplexer #(.width(32)) multiplexer_3 (
    .in0(out_9), .in1(ext_1_out_3), .out(multiplexer_3_out), .sel(Bsel));  // open: en
  // Probe on dm_1_rd
  ALU alu_1 (.A(grf_1_rd1), .B(multiplexer_3_out), .ALUop(ALUop), .Zero(Zero), .LessZero(LessZero), .ans(out_6));
  DM dm_1 (.Addr(out_6), .WD(out_9), .DMwrite(out_4), .clk(clk), .reset(in_1), .RD(dm_1_rd), .in_6(ctrl_1_out_11));

  // Other names for the same wires on the sheet: DMwr = out_4; Instr[31:0] = out_3; MemAddr[31:0] = out_6;
  //   MemData[31:0] = out_9; RegAddr[4:0] = out_8; RegData[31:0] = out_2; reset = in_1; WE = out_7
endmodule

module IFU (
  input  [31:0] NPC,
  input  clk,
  input  reset,
  output [31:0] Instr,
  output [31:0] out_5
);

  wire [11:0] shifter_1_out;
  wire [31:12] shifter_1_out_2;

  Register #(.width(32)) register_1 (.D(NPC), .Q(out_5), .clk(clk), .clr(reset));  // open: en
  // Probe on shifter_1_out
  Shifter #(.width(32), .shift("lr")) shifter_1 (.in(out_5), .\dist (5'b00010), .out({shifter_1_out_2, shifter_1_out}));
  ROM #(.addrWidth(12), .dataWidth(32)) rom_1 (.addr(shifter_1_out), .data(Instr));  // open: sel

  // Notes on the sheet:
  //   contents of rom_1 (hex, n*v repeats v):
  //   34000001 34010001 34020001 34030001 34040001 34050001 34060001 34070001 34080001 34090001 340a0001
  //   340b0001 340c0001 340d0001 340e0001 340f0001 34100001 34110001 34120001 34130001 34140001 34150001
  //   34160001 34170001 34180001 34190001 341a0001 341b0001 341c0001 341d0001 341e0001 341f0001 3404007b
  //   348501c8 3c06007b 3c07ffff 34e7ffff 00868020 00878820 00e79020 34080000 ad040000 ad050004 ad060008
  //   ad07000c ad100010 ad110014 ad120018 8d040000 8d05000c ad04001c ad050020 34040001 34050002 34060001
  //   10850001 10860001 ad040024 ad050028
endmodule

module GRF (
  input  in_1,
  input  [4:0] in_2,
  input  [4:0] in_3,
  input  [4:0] in_4,
  input  [31:0] in_5,
  input  in_6,
  input  in_7,
  output [31:0] RD1,
  output [31:0] RD2
);

  wire and_1_out, and_2_out, and_3_out, and_4_out, and_5_out, and_6_out, and_7_out, and_8_out, and_9_out,
       and_10_out, and_11_out, and_12_out, and_13_out, and_14_out, and_15_out, and_16_out, and_17_out,
       and_18_out, and_19_out, and_20_out, and_21_out, and_22_out, and_23_out, and_24_out, and_25_out,
       and_26_out, and_27_out, and_28_out, and_29_out, and_30_out, and_31_out, and_32_out, w0, w1, w2, w3,
       w4, w5, w6, w7, w8, w9, w10, w11, w12, w13, w14, w15, w16, w17, w18, w19, w20, w21, w22, w23, w24,
       w25, w26, w27, w28, w29, w30, w31;
  wire [31:0] Out0, Out1, Out2, Out3, Out4, Out5, Out6, Out7, Out8, Out9, Out10, Out11, Out12, Out13, Out14,
       Out15, Out16, Out17, Out18, Out19, Out20, Out21, Out22, Out23, Out24, Out25, Out26, Out27, Out28,
       Out29, Out30, Out31;

  and and_1 (and_1_out, w0, in_1);
  and and_2 (and_2_out, w1, in_1);
  and and_3 (and_3_out, w2, in_1);
  and and_4 (and_4_out, w3, in_1);
  and and_5 (and_5_out, w16, in_1);
  and and_6 (and_6_out, w17, in_1);
  and and_7 (and_7_out, w18, in_1);
  and and_8 (and_8_out, w19, in_1);
  Register #(.width(32)) register_1 (.D(in_5), .en(and_1_out), .Q(Out0), .clk(in_6), .clr(in_7));
  Register #(.width(32)) register_2 (.D(in_5), .en(and_2_out), .Q(Out1), .clk(in_6), .clr(in_7));
  Register #(.width(32)) register_3 (.D(in_5), .en(and_3_out), .Q(Out2), .clk(in_6), .clr(in_7));
  Register #(.width(32)) register_4 (.D(in_5), .en(and_4_out), .Q(Out3), .clk(in_6), .clr(in_7));
  Register #(.width(32)) register_5 (.D(in_5), .en(and_5_out), .Q(Out16), .clk(in_6), .clr(in_7));
  Register #(.width(32)) register_6 (.D(in_5), .en(and_6_out), .Q(Out17), .clk(in_6), .clr(in_7));
  Register #(.width(32)) register_7 (.D(in_5), .en(and_7_out), .Q(Out18), .clk(in_6), .clr(in_7));
  Register #(.width(32)) register_8 (.D(in_5), .en(and_8_out), .Q(Out19), .clk(in_6), .clr(in_7));
  Multiplexer #(.select(5), .width(32)) multiplexer_1 (
    .in0({32{1'b0}}), .in1(Out1), .in2(Out2), .in3(Out3), .in4(Out4), .in5(Out5), .in6(Out6), .in7(Out7),
    .in8(Out8), .in9(Out9), .in10(Out10), .in11(Out11), .in12(Out12), .in13(Out13), .in14(Out14),
    .in15(Out15), .in16(Out16), .in17(Out17), .in18(Out18), .in19(Out19), .in20(Out20), .in21(Out21),
    .in22(Out22), .in23(Out23), .in24(Out24), .in25(Out25), .in26(Out26), .in27(Out27), .in28(Out28),
    .in29(Out29), .in30(Out30), .in31(Out31), .out(RD1), .sel(in_2));  // open: en
  Multiplexer #(.select(5), .width(32)) multiplexer_2 (
    .in0({32{1'b0}}), .in1(Out1), .in2(Out2), .in3(Out3), .in4(Out4), .in5(Out5), .in6(Out6), .in7(Out7),
    .in8(Out8), .in9(Out9), .in10(Out10), .in11(Out11), .in12(Out12), .in13(Out13), .in14(Out14),
    .in15(Out15), .in16(Out16), .in17(Out17), .in18(Out18), .in19(Out19), .in20(Out20), .in21(Out21),
    .in22(Out22), .in23(Out23), .in24(Out24), .in25(Out25), .in26(Out26), .in27(Out27), .in28(Out28),
    .in29(Out29), .in30(Out30), .in31(Out31), .out(RD2), .sel(in_3));  // open: en
  Decoder #(.select(5)) decoder_1 (
    .out0(w0), .out1(w1), .out2(w2), .out3(w3), .out4(w4), .out5(w5), .out6(w6), .out7(w7), .out8(w8),
    .out9(w9), .out10(w10), .out11(w11), .out12(w12), .out13(w13), .out14(w14), .out15(w15), .out16(w16),
    .out17(w17), .out18(w18), .out19(w19), .out20(w20), .out21(w21), .out22(w22), .out23(w23), .out24(w24),
    .out25(w25), .out26(w26), .out27(w27), .out28(w28), .out29(w29), .out30(w30), .out31(w31), .sel(in_4));  // open: en
  and and_9 (and_9_out, w4, in_1);
  and and_10 (and_10_out, w5, in_1);
  and and_11 (and_11_out, w6, in_1);
  and and_12 (and_12_out, w7, in_1);
  and and_13 (and_13_out, w20, in_1);
  and and_14 (and_14_out, w21, in_1);
  and and_15 (and_15_out, w22, in_1);
  and and_16 (and_16_out, w23, in_1);
  Register #(.width(32)) register_9 (.D(in_5), .en(and_9_out), .Q(Out4), .clk(in_6), .clr(in_7));
  Register #(.width(32)) register_10 (.D(in_5), .en(and_10_out), .Q(Out5), .clk(in_6), .clr(in_7));
  Register #(.width(32)) register_11 (.D(in_5), .en(and_11_out), .Q(Out6), .clk(in_6), .clr(in_7));
  Register #(.width(32)) register_12 (.D(in_5), .en(and_12_out), .Q(Out7), .clk(in_6), .clr(in_7));
  Register #(.width(32)) register_13 (.D(in_5), .en(and_13_out), .Q(Out20), .clk(in_6), .clr(in_7));
  Register #(.width(32)) register_14 (.D(in_5), .en(and_14_out), .Q(Out21), .clk(in_6), .clr(in_7));
  Register #(.width(32)) register_15 (.D(in_5), .en(and_15_out), .Q(Out22), .clk(in_6), .clr(in_7));
  Register #(.width(32)) register_16 (.D(in_5), .en(and_16_out), .Q(Out23), .clk(in_6), .clr(in_7));
  and and_17 (and_17_out, w8, in_1);
  and and_18 (and_18_out, w9, in_1);
  and and_19 (and_19_out, w10, in_1);
  and and_20 (and_20_out, w11, in_1);
  and and_21 (and_21_out, w24, in_1);
  and and_22 (and_22_out, w25, in_1);
  and and_23 (and_23_out, w26, in_1);
  and and_24 (and_24_out, w27, in_1);
  Register #(.width(32)) register_17 (.D(in_5), .en(and_17_out), .Q(Out8), .clk(in_6), .clr(in_7));
  Register #(.width(32)) register_18 (.D(in_5), .en(and_18_out), .Q(Out9), .clk(in_6), .clr(in_7));
  Register #(.width(32)) register_19 (.D(in_5), .en(and_19_out), .Q(Out10), .clk(in_6), .clr(in_7));
  Register #(.width(32)) register_20 (.D(in_5), .en(and_20_out), .Q(Out11), .clk(in_6), .clr(in_7));
  Register #(.width(32)) register_21 (.D(in_5), .en(and_21_out), .Q(Out24), .clk(in_6), .clr(in_7));
  Register #(.width(32)) register_22 (.D(in_5), .en(and_22_out), .Q(Out25), .clk(in_6), .clr(in_7));
  Register #(.width(32)) register_23 (.D(in_5), .en(and_23_out), .Q(Out26), .clk(in_6), .clr(in_7));
  Register #(.width(32)) register_24 (.D(in_5), .en(and_24_out), .Q(Out27), .clk(in_6), .clr(in_7));
  and and_25 (and_25_out, w12, in_1);
  and and_26 (and_26_out, w13, in_1);
  and and_27 (and_27_out, w14, in_1);
  and and_28 (and_28_out, w15, in_1);
  Register #(.width(32)) register_25 (.D(in_5), .en(and_29_out), .Q(Out28), .clk(in_6), .clr(in_7));
  and and_29 (and_29_out, w28, in_1);
  Register #(.width(32)) register_26 (.D(in_5), .en(and_30_out), .Q(Out29), .clk(in_6), .clr(in_7));
  and and_30 (and_30_out, w29, in_1);
  Register #(.width(32)) register_27 (.D(in_5), .en(and_31_out), .Q(Out30), .clk(in_6), .clr(in_7));
  and and_31 (and_31_out, w30, in_1);
  Register #(.width(32)) register_28 (.D(in_5), .en(and_32_out), .Q(Out31), .clk(in_6), .clr(in_7));
  and and_32 (and_32_out, w31, in_1);
  Register #(.width(32)) register_29 (.D(in_5), .en(and_25_out), .Q(Out12), .clk(in_6), .clr(in_7));
  Register #(.width(32)) register_30 (.D(in_5), .en(and_26_out), .Q(Out13), .clk(in_6), .clr(in_7));
  Register #(.width(32)) register_31 (.D(in_5), .en(and_27_out), .Q(Out14), .clk(in_6), .clr(in_7));
  Register #(.width(32)) register_32 (.D(in_5), .en(and_28_out), .Q(Out15), .clk(in_6), .clr(in_7));

  // Other names for the same wires on the sheet: A1[4:0] = in_2; A2[4:0] = in_3; A3[4:0] = in_4; clk = in_6;
  //   reset = in_7; WD[31:0] = in_5; WE = in_1
endmodule

module ALU (
  input  [2:0] ALUop,
  input  [31:0] A,
  input  [31:0] B,
  output [31:0] ans,
  output Zero,
  output LessZero
);

  wire [31:0] adder_1_out, or_1_out, shifter_1_out, subtractor_1_out;

  Comparator #(.width(32), .mode("unsigned")) comparator_1 (.a(A), .b(B), .eq(Zero), .lt(LessZero));  // open: gt
  Adder #(.width(32)) adder_1 (.a(A), .b(B), .out(adder_1_out));  // open: cin, cout
  Subtractor #(.width(32)) subtractor_1 (.a(A), .b(B), .out(subtractor_1_out));  // open: bin, bout
  assign or_1_out = A | B;  // OR_Gate or_1, 32 bits wide
  Shifter #(.width(32)) shifter_1 (.in(A), .\dist (B[4:0]), .out(shifter_1_out));
  Multiplexer #(.select(3), .width(32)) multiplexer_1 (
    .in0(adder_1_out), .in1(subtractor_1_out), .in2(or_1_out), .in3(shifter_1_out), .in4({B[15:0], A[15:0]}),
    .out(ans), .sel(ALUop));  // open: in5, in6, in7, en

  // Notes on the sheet:
  //   lui:100
  //   0101
  //   000
  //   001
  //   010
  //   011
endmodule

module NPC (
  input  [31:0] PC,
  input  [25:0] Imm,
  input  Zero,
  input  [2:0] NPCop,
  input  [31:0] rs,
  output [31:0] NPC
);

  wire [15:0] shifter_1_out;
  wire [31:0] adder_1_out, adder_2_out, bit_extender_1_out, bit_extender_2_out, multiplexer_1_out;

  Adder #(.width(32)) adder_1 (.a(32'h4), .b(PC), .out(adder_1_out));  // open: cin, cout
  assign bit_extender_1_out = {{16{shifter_1_out[15]}}, shifter_1_out};  // Bit_Extender bit_extender_1
  Shifter #(.width(16)) shifter_1 (.in(Imm[15:0]), .\dist (4'b0010), .out(shifter_1_out));
  assign bit_extender_2_out = {{4{1'b0}}, {Imm, 2'b00}};  // Bit_Extender bit_extender_2
  Adder #(.width(32)) adder_2 (.a(adder_1_out), .b(bit_extender_1_out), .out(adder_2_out));  // open: cin, cout
  Multiplexer #(.width(32)) multiplexer_1 (
    .in0(adder_1_out), .in1(adder_2_out), .out(multiplexer_1_out), .sel(Zero));  // open: en
  // Probe on adder_1_out
  Multiplexer #(.select(3), .width(32)) multiplexer_2 (
    .in0(adder_1_out), .in1(multiplexer_1_out), .in2(bit_extender_2_out), .in7(rs), .out(NPC), .sel(NPCop));  // open: in3, in4, in5, in6, en

  // Notes on the sheet:
  //   normal
  //   j,jal
  //   010
  //   000
  //   jalr,jr
  //   111
endmodule

module EXT (
  input  [15:0] _0_15,
  input  [1:0] EXTop,
  output [31:0] out_3
);

  wire [31:0] bit_extender_1_out, bit_extender_2_out;

  assign bit_extender_1_out = {{16{1'b0}}, _0_15};  // Bit_Extender bit_extender_1
  assign bit_extender_2_out = {{16{_0_15[15]}}, _0_15};  // Bit_Extender bit_extender_2
  Multiplexer #(.select(2), .width(32)) multiplexer_1 (
    .in0(bit_extender_1_out), .in1(bit_extender_2_out), .out(out_3), .sel(EXTop));  // open: in2, in3, en
endmodule

module DM (
  input  [31:0] Addr,
  input  [31:0] WD,
  input  clk,
  input  reset,
  input  DMwrite,
  input  in_6,
  output [31:0] RD
);

  wire [31:0] ram_1_data;

  RAM #(.addrWidth(12), .dataWidth(32), .bus("separate")) ram_1 (
    .addr(Addr[13:2]), .din(WD), .data(ram_1_data), .str(DMwrite), .clk(clk), .ld(in_6), .clr(reset));  // open: sel
  Multiplexer #(.width(32)) multiplexer_1 (.in0(Addr), .in1(ram_1_data), .out(RD), .sel(in_6));  // open: en

  // Other names for the same wires on the sheet: In[31:0] = WD
endmodule

module CTRL (
  input  [5:0] OPcode,
  input  [5:0] Funct,
  output out_3,
  output out_4,
  output out_5,
  output out_6,
  output out_7,
  output [1:0] out_8,
  output [2:0] out_9,
  output [2:0] out_10,
  output out_11
);

  wire add, add_out, beq, lui, lw, not_1_out, not_2_out, not_3_out, not_4_out, not_5_out, not_6_out,
       not_7_out, not_8_out, not_9_out, not_10_out, not_11_out, not_12_out, ori, special_out, sub, sub_out,
       sw;

  or WRsel (out_3, ori, lw, sw, lui, 1'b0);
  not not_1 (not_1_out, OPcode[5]);
  not not_2 (not_2_out, OPcode[4]);
  not not_3 (not_3_out, OPcode[3]);
  not not_4 (not_4_out, OPcode[2]);
  not not_5 (not_5_out, OPcode[1]);
  not not_6 (not_6_out, OPcode[0]);
  not not_7 (not_7_out, Funct[5]);
  not not_8 (not_8_out, Funct[4]);
  not not_9 (not_9_out, Funct[3]);
  not not_10 (not_10_out, Funct[2]);
  not not_11 (not_11_out, Funct[1]);
  not not_12 (not_12_out, Funct[0]);
  buf EXTop1 (out_8[1], 1'b0);  // OR_Gate
  or WDsel (out_4, add, sub, ori, lui, 1'b0);
  and special (special_out, not_1_out, not_2_out, not_3_out, not_4_out, not_5_out, not_6_out);
  or EXTop0 (out_8[0], lw, sw, 1'b0);
  and u_ori (ori, not_1_out, not_2_out, OPcode[3], OPcode[2], not_5_out, OPcode[0]);
  or WE (out_5, ori, lw, add, sub, lui, 1'b0);
  and u_lw (lw, OPcode[5], not_2_out, not_3_out, not_4_out, OPcode[1], OPcode[0]);
  or Bsel (out_6, lui, sw, lw, ori, 1'b0);
  and u_sw (sw, OPcode[5], not_2_out, OPcode[3], not_4_out, OPcode[1], OPcode[0]);
  or ALU2 (out_9[2], lui, 1'b0);
  or DMwr (out_7, sw, 1'b0);
  and u_beq (beq, not_1_out, not_2_out, not_3_out, OPcode[2], not_5_out, not_6_out);
  or ALU1 (out_9[1], ori, 1'b0);
  and u_add (add_out, Funct[5], not_8_out, not_9_out, not_10_out, not_11_out);
  and and_1 (add, special_out, add_out);
  or ALU0 (out_9[0], sub, beq, 1'b0);
  and u_sub (sub_out, Funct[5], not_8_out, not_9_out, not_10_out, Funct[1]);
  and and_2 (sub, special_out, sub_out);
  buf NPC2 (out_10[2], 1'b0);  // OR_Gate
  buf NPC1 (out_10[1], 1'b0);  // OR_Gate
  and u_lui (lui, not_1_out, not_2_out, OPcode[3], OPcode[2], OPcode[1], OPcode[0]);
  or NPC0 (out_10[0], beq, 1'b0);
  buf MemtoReg (out_11, lw);  // OR_Gate
endmodule
